// Logisim project lab4.3.circ as structural Verilog: 1 circuit, main circuit Adder32
// 加法器
module Adder32 (
  input  Cin,
  input  [31:0] X,
  input  [31:0] Y,
  output CF,
  output Cout,
  output OF,
  output SF,
  output [31:0] S,
  output ZF
);

  wire adder16_2_c16;

  Adder16 adder16_1 (.X(X[31:16]), .Y(Y[31:16]), .C0(adder16_2_c16), .S(S[31:16]), .C16(Cout));  // open: Pg, Gg
  Adder16 adder16_2 (.X(X[15:0]), .Y(Y[15:0]), .C0(Cin), .S(S[15:0]), .C16(adder16_2_c16));  // open: Pg, Gg
  xor xor_1 (CF, Cin, Cout);
  ExactlyOne xor_2 (.out(OF), .in0(Y[31]), .in1(X[31]), .in2(Cout), .in3(S[31]));
  // Probe on X
  // Probe on Y
  // Probe on S
  nor nor_1 (ZF, S[31], S[30], S[29], S[28], S[27], S[26], S[25], S[24], S[23], S[22], S[21], S[20], S[19], S[18], S[17], S[16], S[15], S[14], S[13], S[12], S[11], S[10], S[9], S[8], S[7], S[6], S[5], S[4], S[3], S[2], S[1], S[0]);

  assign SF = S[31];

  // Notes on the sheet:
  //   Y: pull=down
  //   X: pull=down
  //   Cin: pull=down
  //   输入引脚区
  //   输出引脚区
  //   请勿修改引脚名称、电路名称及电路封装外观
  //   提示：使用16位并行加法器子电路实现32位快速加法器
  //   功能说明:32位Adder  S=X+Y，Cout为最高位进位位，Cin为进位输入， S为和，溢出OF、进位CF、零ZF、符号SF。
  //   +
  //   =
  //   无符号加法
endmodule
