// Logisim project lab4.5.circ as structural Verilog: 3 circuits, main circuit ALU
module \符号扩展1_32  (
  input  in_1,
  output [31:0] out_2
);


  assign out_2 = {32{in_1}};
endmodule

module ALU (
  input  [3:0] ALUctr,
  input  [31:0] A,
  input  [31:0] B,
  output Zero,
  output [31:0] S
);

  wire adder32_1_cf, adder32_1_of, adder32_1_sf, aluctrl_1_alctr, aluctrl_1_lrctr, aluctrl_1_sigctr,
       aluctrl_1_subctr, multiplexer_1_out, xor_3_out;
  wire [2:0] aluctrl_1_opctr;
  wire [31:0] adder32_1_s, and_1_out, bit_extender_1_out, bit_extender_2_out, multiplier_1_out, or_1_out,
       shifter32_1_dataout, xor_1_out, xor_2_out;

  assign bit_extender_1_out = {{31{aluctrl_1_subctr}}, aluctrl_1_subctr};  // Bit_Extender bit_extender_1
  assign xor_1_out = B ^ bit_extender_1_out;  // XOR_Gate xor_1, 32 bits wide
  assign and_1_out = A & B;  // AND_Gate and_1, 32 bits wide
  assign or_1_out = A | B;  // OR_Gate or_1, 32 bits wide
  assign xor_2_out = A ^ B;  // XOR_Gate xor_2, 32 bits wide
  Shifter32 shifter32_1 (
    .L_R(aluctrl_1_lrctr), .shamt(B[4:0]), .DataIn(A), .DataOut(shifter32_1_dataout), .A_L(aluctrl_1_alctr));
  Multiplier #(.width(32)) multiplier_1 (.a(A), .b(B), .out(multiplier_1_out));  // open: cin, cout
  Adder32 adder32_1 (
    .Cin(aluctrl_1_subctr), .X(A), .Y(xor_1_out), .S(adder32_1_s), .OF(adder32_1_of), .CF(adder32_1_cf),
    .ZF(Zero), .SF(adder32_1_sf));  // open: Cout
  xor xor_3 (xor_3_out, adder32_1_of, adder32_1_sf);
  // Probe on A
  // Probe on B
  // Probe on S
  Multiplexer #(.enable("false")) multiplexer_1 (
    .in0(adder32_1_cf), .in1(xor_3_out), .out(multiplexer_1_out), .sel(aluctrl_1_sigctr));
  Multiplexer #(.select(3), .width(32), .enable("false")) multiplexer_2 (
    .in0(adder32_1_s), .in1(and_1_out), .in2(or_1_out), .in3(xor_2_out), .in4(shifter32_1_dataout), .in5(B),
    .in6(bit_extender_2_out), .in7(multiplier_1_out), .out(S), .sel(aluctrl_1_opctr));
  ALUctrl aluctrl_1 (
    .SUBctr(aluctrl_1_subctr), .LRctr(aluctrl_1_lrctr), .SIGctr(aluctrl_1_sigctr), .ALctr(aluctrl_1_alctr),
    .OPctr(aluctrl_1_opctr), .ALUctr(ALUctr));
  assign bit_extender_2_out = {{31{1'b0}}, multiplexer_1_out};  // Bit_Extender bit_extender_2

  // Other names for the same wires on the sheet: Result[31:0] = S

  // Notes on the sheet:
  //   ALUctr: pull=down
  //   B: pull=down
  //   A: pull=down
  //   输入引脚
  //   请勿修改引脚名称、电路名称及电路封装外观
  //   提示：使用32位并行加法器子电路、桶形移位器、ALU控制子电路实现32位ALU
  //   功能说明:32位ALU，输入32位操作数A、B，4位控制信号ALUctr，输出32位结果Reseult和1位Zero标志位
  //   输出引脚
  //   操作数和结果
endmodule

module ALUctrl (
  input  [3:0] ALUctr,
  output SUBctr,
  output LRctr,
  output SIGctr,
  output ALctr,
  output [2:0] OPctr
);

  wire decoder_1_out3, decoder_1_out4, decoder_1_out5, decoder_1_out6, decoder_1_out7, decoder_1_out8,
       decoder_1_out15;

  Decoder #(.select(4), .enable("false")) decoder_1 (
    .out1(LRctr), .out2(SIGctr), .out3(decoder_1_out3), .out4(decoder_1_out4), .out5(decoder_1_out5),
    .out6(decoder_1_out6), .out7(decoder_1_out7), .out8(decoder_1_out8), .out13(ALctr),
    .out15(decoder_1_out15), .sel(ALUctr));  // open: out0, out9, out10, out11, out12, out14
  or or_1 (OPctr[0], decoder_1_out4, decoder_1_out7, decoder_1_out15);
  or or_2 (OPctr[1], SIGctr, decoder_1_out3, decoder_1_out4, decoder_1_out6);
  or or_3 (OPctr[2], LRctr, SIGctr, decoder_1_out3, decoder_1_out5, ALctr, decoder_1_out15);
  or or_4 (SUBctr, SIGctr, decoder_1_out3, decoder_1_out8);

  // Notes on the sheet:
  //   输入引脚
  //   ALU操作控制信号生成部件
  //   输出引脚
endmodule
