// Logisim project lab4.think1.circ as structural Verilog: 1 circuit, main circuit main
module main (
  input  [31:0] in_1,
  input  [31:0] in_2,
  input  [31:0] in_3,
  input  [31:0] in_4,
  input  in_5,
  output [31:0] out_6,
  output C64,
  output Pg,
  output Gg,
  output [31:0] out_10
);

  wire adder16_1_gg, adder16_1_pg, adder16_2_gg, adder16_2_pg, adder16_3_gg, adder16_3_pg, adder16_4_gg,
       adder16_4_pg, clu4_1_c1, clu4_1_c2, clu4_1_c3;

  Adder16 adder16_1 (
    .X(in_1[15:0]), .Y(in_2[15:0]), .C0(in_5), .S(out_10[31:16]), .Pg(adder16_1_pg), .Gg(adder16_1_gg));  // open: C16
  Adder16 adder16_2 (
    .X(in_1[31:16]), .Y(in_2[31:16]), .C0(clu4_1_c1), .S(out_10[15:0]), .Pg(adder16_2_pg), .Gg(adder16_2_gg));  // open: C16
  CLU4 clu4_1 (
    .P0(adder16_1_pg), .P1(adder16_2_pg), .P2(adder16_3_pg), .P3(adder16_4_pg), .C1(clu4_1_c1),
    .C3(clu4_1_c3), .G0(adder16_1_gg), .G1(adder16_2_gg), .G2(adder16_3_gg), .G3(adder16_4_gg),
    .C2(clu4_1_c2), .C4(C64), .C0(in_5), .Pg(Pg), .Gg(Gg));
  Adder16 adder16_3 (
    .X(in_3[15:0]), .Y(in_4[15:0]), .C0(clu4_1_c2), .S(out_6[31:16]), .Pg(adder16_3_pg), .Gg(adder16_3_gg));  // open: C16
  Adder16 adder16_4 (
    .X(in_3[31:16]), .Y(in_4[31:16]), .C0(clu4_1_c3), .S(out_6[15:0]), .Pg(adder16_4_pg), .Gg(adder16_4_gg));  // open: C16

  // Other names for the same wires on the sheet: C0 = in_5; x0[31:0] = in_1; x1[31:0] = in_3; y0[31:0] = in_2;
  //   y1[31:0] = in_4; z0[31:0] = out_6; z1[31:0] = out_10
endmodule
