// Logisim project lab4.think2.circ as structural Verilog: 1 circuit, main circuit main
module main (
  input  in_1,
  input  [31:0] in_2,
  input  in_3,
  input  [31:0] in_4,
  output [31:0] out_5,
  output out_6,
  output [31:0] out_7,
  output out_8
);

  wire not_1_out, or_1_out;
  wire [6:0] counter_1_q;
  wire [31:0] adder32_1_s, multiplexer_1_out, multiplexer_2_out;
  wire [31:31] adder32_1_cout;

  not not_1 (not_1_out, out_8);
  Multiplexer #(.width(32), .enable("false")) multiplexer_1 (
    .in0({32{1'b0}}), .in1(in_2), .out(multiplexer_1_out), .sel(out_7[0]));
  Adder32 adder32_1 (
    .Cin(1'b0), .Cout(adder32_1_cout[31]), .X(multiplexer_1_out), .Y(out_5), .S(adder32_1_s));  // open: OF, CF, ZF, SF
  Register #(.width(32), .Select("low")) register_1 (
    .D({adder32_1_cout[31], adder32_1_s[31:1]}), .en(not_1_out), .Q(out_5), .clk(in_1), .clr(in_3));
  Multiplexer #(.width(32), .enable("false")) multiplexer_2 (
    .in0({adder32_1_s[0], out_7[31:1]}), .in1(in_4), .out(multiplexer_2_out), .sel(out_6));
  Register #(.width(32), .Select("low")) register_2 (
    .D(multiplexer_2_out), .en(not_1_out), .Q(out_7), .clk(in_1), .clr(in_3));
  or or_1 (or_1_out, in_3, not_1_out);
  Counter #(.width(7), .max('h7f)) counter_1 (
    .load(1'b0), .D({7{1'b0}}), .count(or_1_out), .Q(counter_1_q), .clk(in_1), .clr(in_3), .down(1'b0));  // open: carry, preset
  Comparator #(.width(7)) comparator_1 (.a(counter_1_q), .b({7{1'b0}}), .eq(out_6));  // open: gt, lt
  Comparator #(.width(7)) comparator_2 (.a(counter_1_q), .b(7'b0100001), .eq(out_8));  // open: gt, lt

  // Other names for the same wires on the sheet: clock = in_1; load = out_6; reset = in_3; stop = out_8;
  //   x[31:0] = in_2; y[31:0] = in_4; Z0[31:0] = out_5; Z1[31:0] = out_7
endmodule
