// Logisim project lab5.2.circ as structural Verilog: 2 circuits, main circuit DataRam
// DataRAM
module DataRam (
  input  CLK,
  input  CLR,
  input  WE,
  input  [2:0] MemOp,
  input  [17:0] Addr,
  input  [31:0] Din,
  output AlignErr,
  output [31:0] DataOut
);

  wire [3:0] SEL;
  wire [7:0] IN0, IN1, IN2, IN3, OUT0, OUT1, OUT2, OUT3;
  wire [31:0] bit_extender_1_out, bit_extender_2_out, bit_extender_3_out, bit_extender_4_out,
       bit_extender_5_out, bit_extender_6_out, bit_extender_7_out, bit_extender_8_out, bit_extender_9_out,
       bit_extender_10_out, bit_extender_11_out, bit_extender_12_out, multiplexer_1_out, multiplexer_2_out,
       multiplexer_3_out, multiplexer_4_out, multiplexer_5_out, multiplexer_6_out;

  \逻辑控制  \u_逻辑控制_1  (.MemOp(MemOp), .Add01(Addr[1:0]), .out_3({SEL, AlignErr}));
  RAM #(.addrWidth(16), .bus("separate"), .Select("high")) ram_1 (
    .addr(Addr[17:2]), .din(IN0), .data(OUT0), .str(WE), .sel(SEL[0]), .clk(CLK), .clr(CLR));  // open: ld
  RAM #(.addrWidth(16), .bus("separate"), .Select("high")) ram_2 (
    .addr(Addr[17:2]), .din(IN1), .data(OUT1), .str(WE), .sel(SEL[1]), .clk(CLK), .clr(CLR));  // open: ld
  RAM #(.addrWidth(16), .bus("separate"), .Select("high")) ram_3 (
    .addr(Addr[17:2]), .din(IN2), .data(OUT2), .str(WE), .sel(SEL[2]), .clk(CLK), .clr(CLR));  // open: ld
  RAM #(.addrWidth(16), .bus("separate"), .Select("high")) ram_4 (
    .addr(Addr[17:2]), .din(IN3), .data(OUT3), .str(WE), .sel(SEL[3]), .clk(CLK), .clr(CLR));  // open: ld
  assign bit_extender_1_out = {{24{1'b0}}, OUT0};  // Bit_Extender bit_extender_1
  assign bit_extender_2_out = {{24{OUT0[7]}}, OUT0};  // Bit_Extender bit_extender_2
  assign bit_extender_3_out = {{24{1'b0}}, OUT1};  // Bit_Extender bit_extender_3
  assign bit_extender_4_out = {{24{OUT1[7]}}, OUT1};  // Bit_Extender bit_extender_4
  assign bit_extender_5_out = {{24{1'b0}}, OUT2};  // Bit_Extender bit_extender_5
  assign bit_extender_6_out = {{24{OUT2[7]}}, OUT2};  // Bit_Extender bit_extender_6
  assign bit_extender_7_out = {{24{1'b0}}, OUT3};  // Bit_Extender bit_extender_7
  assign bit_extender_8_out = {{24{OUT3[7]}}, OUT3};  // Bit_Extender bit_extender_8
  assign bit_extender_9_out = {{16{1'b0}}, {OUT1, OUT0}};  // Bit_Extender bit_extender_9
  assign bit_extender_10_out = {{16{OUT1[7]}}, {OUT1, OUT0}};  // Bit_Extender bit_extender_10
  assign bit_extender_11_out = {{16{1'b0}}, {OUT3, OUT2}};  // Bit_Extender bit_extender_11
  assign bit_extender_12_out = {{16{OUT3[7]}}, {OUT3, OUT2}};  // Bit_Extender bit_extender_12
  Multiplexer #(.width(32), .enable("false")) multiplexer_1 (
    .in0(bit_extender_1_out), .in1(bit_extender_2_out), .out(multiplexer_1_out), .sel(MemOp[2]));
  Multiplexer #(.width(32), .enable("false")) multiplexer_2 (
    .in0(bit_extender_3_out), .in1(bit_extender_4_out), .out(multiplexer_2_out), .sel(MemOp[2]));
  Multiplexer #(.width(32), .enable("false")) multiplexer_3 (
    .in0(bit_extender_5_out), .in1(bit_extender_6_out), .out(multiplexer_3_out), .sel(MemOp[2]));
  Multiplexer #(.width(32), .enable("false")) multiplexer_4 (
    .in0(bit_extender_7_out), .in1(bit_extender_8_out), .out(multiplexer_4_out), .sel(MemOp[2]));
  Multiplexer #(.width(32), .enable("false")) multiplexer_5 (
    .in0(bit_extender_9_out), .in1(bit_extender_10_out), .out(multiplexer_5_out), .sel(MemOp[2]));
  Multiplexer #(.width(32), .enable("false")) multiplexer_6 (
    .in0(bit_extender_11_out), .in1(bit_extender_12_out), .out(multiplexer_6_out), .sel(MemOp[2]));
  Multiplexer #(.select(4), .width(32), .enable("false")) multiplexer_7 (
    .in1(multiplexer_1_out), .in2(multiplexer_2_out), .in3(multiplexer_5_out), .in4(multiplexer_3_out),
    .in8(multiplexer_4_out), .in12(multiplexer_6_out), .in15({OUT3, OUT2, OUT1, OUT0}), .out(DataOut),
    .sel(SEL));  // open: in0, in5, in6, in7, in9, in10, in11, in13, in14
  Multiplexer #(.select(4), .width(8), .enable("false")) multiplexer_8 (
    .in8(Din[7:0]), .in12(Din[15:8]), .in15(Din[31:24]), .out(IN3), .sel(SEL));  // open: in0, in1, in2, in3, in4, in5, in6, in7, in9, in10, in11, in13, in14
  Multiplexer #(.select(4), .width(8), .enable("false")) multiplexer_9 (
    .in4(Din[7:0]), .in12(Din[7:0]), .in15(Din[23:16]), .out(IN2), .sel(SEL));  // open: in0, in1, in2, in3, in5, in6, in7, in8, in9, in10, in11, in13, in14
  Multiplexer #(.select(4), .width(8), .enable("false")) multiplexer_10 (
    .in2(Din[7:0]), .in3(Din[15:8]), .in15(Din[15:8]), .out(IN1), .sel(SEL));  // open: in0, in1, in4, in5, in6, in7, in8, in9, in10, in11, in12, in13, in14
  Multiplexer #(.select(4), .width(8), .enable("false")) multiplexer_11 (
    .in1(Din[7:0]), .in3(Din[7:0]), .in15(Din[7:0]), .out(IN0), .sel(SEL));  // open: in0, in2, in4, in5, in6, in7, in8, in9, in10, in11, in12, in13, in14

  // Other names for the same wires on the sheet: Dout[31:0] = DataOut; ma[4:0] = {MemOp, Addr[1:0]}

  // Notes on the sheet:
  //   输入引脚
  //   请勿修改引脚名称、电路名称及电路封装外观
  //   为了后续实验中的引用，不要修改MemOp的编码定义、引脚名称和在布局中的位置。
  //   32位数据存储器，按字节分4片存储，可按照字节、半字和字进行存储；读取字节或半字时，支持0扩展和符号位扩展。
  //   输出引脚
endmodule

module \逻辑控制  (
  input  [2:0] MemOp,
  input  [1:0] Add01,
  output [4:0] out_3
);

  ROM #(.addrWidth(5), .dataWidth(5), .Select("low")) rom_1 (.addr({MemOp, Add01}), .data(out_3), .sel(1'b0));

  // Notes on the sheet:
  //   contents of rom_1 (hex, n*v repeats v):
  //   1e 1 1 1 2 4 8 10 6 1 18 9*1 2 4 8 10 6 1 18 5*1
endmodule
