// Logisim project lab5.5.circ as structural Verilog: 2 circuits, main circuit main
module main (
  input  [2:0] ExtOp,
  input  [2:0] MemOp,
  input  RegWr,
  input  ALUASrc,
  input  MemWr,
  input  [1:0] ALUBSrc,
  input  [31:0] Initial_Address,
  input  [3:0] ALUctr,
  input  MemtoReg,
  input  [2:0] BandJ,
  input  clk,
  input  ReSet,
  output [31:0] PC,
  output [31:0] BusW,
  output [31:0] Din,
  output NPCASrc,
  output NPCBSrc
);

  wire zero;
  wire [31:0] BusA, DataA, DataB, dataram_1_dataout, Imm, IR, resultl;

  BandJ bandj_1 (.Branch(BandJ), .NxtASrc(NPCASrc), .Zero(zero), .NxtBSrc(NPCBSrc), .Result0(resultl[0]));
  IDU idu_1 (
    .ExtOp(ExtOp), .RegWr(RegWr), .ALUASrc(ALUASrc), .ALUBSrc(ALUBSrc), .IR(IR), .BusW(BusW), .PC(PC),
    .DataA(DataA), .BusB(Din), .DataB(DataB), .Imm(Imm), .BusA(BusA), .CLK(clk));  // open: OpCode, Funct3, Funct7
  ALU alu_1 (.A(DataA), .B(DataB), .ALUctr(ALUctr), .S(resultl), .Zero(zero));
  IFU ifu_1 (
    .PC(PC), .Initial_Address(Initial_Address), .BusA(BusA), .NPCASrc(NPCASrc), .NPCBSrc(NPCBSrc), .Imm(Imm),
    .CLK(clk), .Reset(ReSet));  // open: IR
  DataRam dataram_1 (
    .Addr(resultl[17:0]), .Din(Din), .DataOut(dataram_1_dataout), .CLK(clk), .CLR(ReSet), .MemOp(MemOp),
    .WE(MemWr));  // open: AlignErr
  ROM #(.addrWidth(16), .dataWidth(32), .Select("high"), .simpleMode("false")) rom_1 (
    .addr(PC[17:2]), .data(IR), .sel(1'b1));
  Multiplexer #(.width(32), .enable("false")) multiplexer_1 (
    .in0(resultl), .in1(dataram_1_dataout), .out(BusW), .sel(MemtoReg));

  // Other names for the same wires on the sheet: BusB[31:0] = Din; Init_Addr[31:0] = Initial_Address

  // Notes on the sheet:
  //   ALUASrc: pull=down
  //   BandJ: pull=down
  //   RegWr: pull=down
  //   NPCASrc: pull=down
  //   ALUBSrc: pull=down
  //   ALUctr: pull=down
  //   ExtOp: pull=down
  //   NPCBSrc: pull=down
  //   输入信号
  //   请勿修改引脚名称、电路名称及电路封装外观
  //   为了后续实验中的引用，不要修改控制信号的编码定义、引脚名称和在布局中的位置。
  //   指令存储器和数据存储器数据位都是32位，指令存储器编址以字为单位，数据存储器编址以字节为单位。
  //   32位数据存储器，按字节分4片存储，可按照字节、半字和字进行存储；读取字节或半字时，支持0扩展和符号位扩展。
  //   输出信号
  //   contents of rom_1 (hex, n*v repeats v):
  //   256*0 fedca2b7 f9c28293 1006013 6502223 6400303 6601423 6405383 6701623 4042d413 6444b3 649533
  //   8505b3 b2a633 b2b6b3 40b287b3 6f02823 67c263 67d263 40086f 4808e7 1917
endmodule

module BandJ (
  input  [2:0] Branch,
  input  Zero,
  input  Result0,
  output NxtASrc,
  output NxtBSrc
);

  wire not_1_out, or_1_out;

  not not_1 (not_1_out, Zero);
  or or_1 (or_1_out, ~Result0, Zero);  // OR_Gate
  Multiplexer #(.select(3), .enable("false")) multiplexer_1 (
    .in0(1'b0), .in1(1'b0), .in2(1'b1), .in4(1'b0), .in5(1'b0), .in6(1'b0), .in7(1'b0), .out(NxtASrc),
    .sel(Branch));  // open: in3
  Multiplexer #(.select(3), .enable("false")) multiplexer_2 (
    .in0(1'b0), .in1(1'b1), .in2(1'b1), .in4(Zero), .in5(not_1_out), .in6(Result0), .in7(or_1_out),
    .out(NxtBSrc), .sel(Branch));  // open: in3

  // Notes on the sheet:
  //   Zero: pull=down
  //   Branch: pull=down
  //   输入信号
  //   请勿修改引脚名称、电路名称及电路封装外观
  //   不要修改控制信号的编码定义、引脚名称和在布局中的位置。
  //   输出信号
endmodule
