// Logisim project lab5.think1.circ as structural Verilog: 1 circuit, main circuit main
module main (
);

  wire clock_1_out;
  wire [2:0] control;
  wire [6:0] multiplexer_1_out, multiplexer_2_out, multiplexer_3_out;
  wire [7:0] main_1_row1, main_1_row2, main_1_row3, main_1_row4, main_1_row5, main_1_row6, main_1_row7,
       main_1_row8, main_1_row9, main_1_row10, main_1_row11, main_1_row12, main_1_row13, main_1_row14,
       main_1_row15, main_1_row16, main_2_row1, main_2_row2, main_2_row3, main_2_row4, main_2_row5,
       main_2_row6, main_2_row7, main_2_row8, main_2_row9, main_2_row10, main_2_row11, main_2_row12,
       main_2_row13, main_2_row14, main_2_row15, main_2_row16, main_3_row1, main_3_row2, main_3_row3,
       main_3_row4, main_3_row5, main_3_row6, main_3_row7, main_3_row8, main_3_row9, main_3_row10,
       main_3_row11, main_3_row12, main_3_row13, main_3_row14, main_3_row15, main_3_row16;

  Counter #(.width(3), .max('h4)) counter_1 (
    .Q(control), .clk(clock_1_out));  // open: load, D, count, carry, clr, preset, down
  Clock clock_1 (.out(clock_1_out));
  Multiplexer #(.select(3), .width(7), .enable("false")) multiplexer_1 (
    .in0(7'b0110000), .in1(7'b0110001), .in2(7'b0110010), .in3(7'b0110011), .in4(7'b0110100),
    .out(multiplexer_1_out), .sel(control));  // open: in5, in6, in7
  Multiplexer #(.select(3), .width(7), .enable("false")) multiplexer_2 (
    .in0(7'b0110001), .in1(7'b0110010), .in2(7'b0110011), .in3(7'b0110100), .in4(7'b0110000),
    .out(multiplexer_2_out), .sel(control));  // open: in5, in6, in7
  Multiplexer #(.select(3), .width(7), .enable("false")) multiplexer_3 (
    .in0(7'b0110010), .in1(7'b0110011), .in2(7'b0110100), .in3(7'b0110000), .in4(7'b0110001),
    .out(multiplexer_3_out), .sel(control));  // open: in5, in6, in7
  DotMatrix #(.inputtype("row"), .matrixcols(8), .matrixrows(16)) dotmatrix_1 (
    .row0(main_1_row1), .row1(main_1_row2), .row2(main_1_row3), .row3(main_1_row4), .row4(main_1_row5),
    .row5(main_1_row6), .row6(main_1_row7), .row7(main_1_row8), .row8(main_1_row9), .row9(main_1_row10),
    .row10(main_1_row11), .row11(main_1_row12), .row12(main_1_row13), .row13(main_1_row14),
    .row14(main_1_row15), .row15(main_1_row16));
  lab5_1_main main_1 (
    .ASCII_CODE(multiplexer_1_out), .row1(main_1_row1), .row2(main_1_row2), .row3(main_1_row3),
    .row4(main_1_row4), .row7(main_1_row7), .row5(main_1_row5), .row6(main_1_row6), .row8(main_1_row8),
    .row9(main_1_row9), .row10(main_1_row10), .row11(main_1_row11), .row12(main_1_row12),
    .row13(main_1_row13), .row14(main_1_row14), .row15(main_1_row15), .row16(main_1_row16));  // open: CodeErr
  lab5_1_main main_2 (
    .ASCII_CODE(multiplexer_2_out), .row1(main_2_row1), .row2(main_2_row2), .row3(main_2_row3),
    .row4(main_2_row4), .row7(main_2_row7), .row5(main_2_row5), .row6(main_2_row6), .row8(main_2_row8),
    .row9(main_2_row9), .row10(main_2_row10), .row11(main_2_row11), .row12(main_2_row12),
    .row13(main_2_row13), .row14(main_2_row14), .row15(main_2_row15), .row16(main_2_row16));  // open: CodeErr
  DotMatrix #(.inputtype("row"), .matrixcols(8), .matrixrows(16)) dotmatrix_2 (
    .row0(main_2_row1), .row1(main_2_row2), .row2(main_2_row3), .row3(main_2_row4), .row4(main_2_row5),
    .row5(main_2_row6), .row6(main_2_row7), .row7(main_2_row8), .row8(main_2_row9), .row9(main_2_row10),
    .row10(main_2_row11), .row11(main_2_row12), .row12(main_2_row13), .row13(main_2_row14),
    .row14(main_2_row15), .row15(main_2_row16));
  DotMatrix #(.inputtype("row"), .matrixcols(8), .matrixrows(16)) dotmatrix_3 (
    .row0(main_3_row1), .row1(main_3_row2), .row2(main_3_row3), .row3(main_3_row4), .row4(main_3_row5),
    .row5(main_3_row6), .row6(main_3_row7), .row7(main_3_row8), .row8(main_3_row9), .row9(main_3_row10),
    .row10(main_3_row11), .row11(main_3_row12), .row12(main_3_row13), .row13(main_3_row14),
    .row14(main_3_row15), .row15(main_3_row16));
  lab5_1_main main_3 (
    .ASCII_CODE(multiplexer_3_out), .row1(main_3_row1), .row2(main_3_row2), .row3(main_3_row3),
    .row4(main_3_row4), .row7(main_3_row7), .row5(main_3_row5), .row6(main_3_row6), .row8(main_3_row8),
    .row9(main_3_row9), .row10(main_3_row10), .row11(main_3_row11), .row12(main_3_row12),
    .row13(main_3_row13), .row14(main_3_row14), .row15(main_3_row15), .row16(main_3_row16));  // open: CodeErr
endmodule
