// Logisim project lab6.1.circ as structural Verilog: 1 circuit, main circuit 控制器
module \控制器  (
  input  [6:0] opcode,
  input  [2:0] funct3,
  input  [6:0] funct7,
  output [2:0] ExtOp,
  output RegWr,
  output [2:0] BandJ,
  output ALUASrc,
  output [1:0] ALUBSrc,
  output [3:0] ALUctr,
  output MemtoReg,
  output [2:0] MemOp,
  output MemWr
);

  wire and_1_out, and_2_out, Halt, high, isB, isI, isJair, isJal, isR, isUaui, isUlui, or_2_out;
  wire [0:0] or_5_out;
  wire [2:0] Memtemp, multiplexer_4_out;
  wire [3:0] ALUtemp, multiplexer_5_out;
  wire [3:3] or_4_out;

  Comparator #(.width(7)) comparator_1 (.a(opcode), .b(7'b0110111), .eq(isUlui));  // open: gt, lt
  Comparator #(.width(7)) comparator_2 (.a(opcode), .b(7'b0010111), .eq(isUaui));  // open: gt, lt
  or or_1 (RegWr, isUlui, isUaui, isJair, isJal, isI, isR, MemtoReg);
  Multiplexer #(.select(3), .width(3), .enable("false")) multiplexer_1 (
    .in0(3'b101), .in1(3'b110), .in2(3'b000), .in4(3'b001), .in5(3'b010), .out(Memtemp), .sel(funct3));  // open: in3, in6, in7
  Multiplexer #(.width(3), .enable("false")) multiplexer_2 (.in0(3'b000), .in1(Memtemp), .out(MemOp), .sel(or_2_out));
  or or_2 (or_2_out, MemtoReg, MemWr);
  and and_1 (and_1_out, funct7[5], isR);
  or or_3 (high, and_1_out, and_2_out);
  and and_2 (and_2_out, funct7[5], funct3[0], ~funct3[1], funct3[2], isI);  // AND_Gate
  Comparator #(.width(7)) comparator_3 (.a(opcode), .b(7'b1100111), .eq(isJair));  // open: gt, lt
  Comparator #(.width(7)) comparator_4 (.a(opcode), .b(7'b1101111), .eq(isJal));  // open: gt, lt
  or or_4 (or_4_out[3], isUlui, isUaui);
  or or_5 (or_5_out[0], isR, isI);
  Comparator #(.width(7)) comparator_5 (.a(opcode), .b(7'b1100011), .eq(isB));  // open: gt, lt
  Comparator #(.width(7)) comparator_6 (.a(opcode), .b(7'b0100011), .eq(MemWr));  // open: gt, lt
  or or_6 (ALUASrc, isUaui, isJair, isJal);
  Multiplexer #(.select(2), .width(4), .enable("false")) multiplexer_3 (
    .in0(4'b0000), .in1({high, funct3}), .in2(4'b1111), .out(ALUtemp), .sel({isUlui, or_5_out[0]}));  // open: in3
  ROM #(.addrWidth(5), .dataWidth(3), .Select("low")) rom_1 (
    .addr({isI, or_4_out[3], MemWr, isB, isJal}), .data(ExtOp));
  Comparator #(.width(7)) comparator_7 (.a(opcode), .b(7'b0010011), .eq(isI));  // open: gt, lt
  Comparator #(.width(7)) comparator_8 (.a(opcode), .b(7'b0000011), .eq(MemtoReg));  // open: gt, lt
  or or_7 (ALUBSrc[1], isUlui, isUaui, MemtoReg, MemWr, isI);
  or or_8 (ALUBSrc[0], isJal, isJair);
  Multiplexer #(.select(3), .width(3), .enable("false")) multiplexer_4 (
    .in0(3'b100), .in1(3'b101), .in4(3'b110), .in5(3'b111), .in6(3'b110), .in7(3'b111),
    .out(multiplexer_4_out), .sel(funct3));  // open: in2, in3
  Multiplexer #(.select(3), .width(4), .enable("false")) multiplexer_5 (
    .in0(4'b0010), .in1(4'b0010), .in4(4'b0010), .in5(4'b0010), .in6(4'b0011), .in7(4'b0011),
    .out(multiplexer_5_out), .sel(funct3));  // open: in2, in3
  Comparator #(.width(7)) comparator_9 (.a(opcode), .b(7'b0110011), .eq(isR));  // open: gt, lt
  Comparator #(.width(7)) comparator_10 (.a(opcode), .b(7'b1110011), .eq(Halt));  // open: gt, lt
  Multiplexer #(.select(3), .width(3), .enable("false")) multiplexer_6 (
    .in0(3'b000), .in1(multiplexer_4_out), .in2(3'b001), .in4(3'b010), .out(BandJ), .sel({isJair, isJal, isB}));  // open: in3, in5, in6, in7
  Multiplexer #(.width(4), .enable("false")) multiplexer_7 (
    .in0(ALUtemp), .in1(multiplexer_5_out), .out(ALUctr), .sel(isB));

  // Other names for the same wires on the sheet: isS = MemWr; isL = MemtoReg

  // Notes on the sheet:
  //   输入引脚
  //   请勿修改引脚名称、电路名称及电路封装外观
  //   提示：根据指令种类，把7位指令code用一位指令类型标志位来表示，再通过功能码来区分具体指令，生成控制信号。
  //   输出引脚
  //   contents of rom_1 (hex, n*v repeats v):
  //   0 4 3 0 2 0 0 0 1
endmodule
